// Logisim project index.circ as structural Verilog: 3 circuits, main circuit main
module main (
  input  clear,
  input  [7:0] in_2,
  input  S0,
  input  S1,
  input  Binvert
);

  wire adder_1_cout, adder_1_out, and_1_out, B_out, Carry_q, clock_1_out, mux_1_output, or_1_out, undriven,
       undriven_2, undriven_3, undriven_4, undriven_5, undriven_6, undriven_7, undriven_8, undriven_9,
       undriven_10, xor_1_out, xor_2_out;
  wire [3:0] B_q3, B_q7, registrador_1_c_out, registrador_1_q3, registrador_2_c_out, registrador_2_q3;

  registrador registrador_1 (
    .C_In(undriven), .Clear(undriven_2), .Clock(clock_1_out), .Preset_0(undriven_3),
    .Q0(registrador_1_q3[3]), .Preset_1(undriven_4), .Q1(registrador_1_q3[2]), .Preset_2(undriven_5),
    .Q2(registrador_1_q3[1]), .Preset_3(undriven_6), .Q3(registrador_1_q3[0]), .Preset_4(undriven_7),
    .Q4(registrador_1_c_out[3]), .Preset_5(undriven_8), .Q5(registrador_1_c_out[2]), .Preset_6(undriven_9),
    .Q6(registrador_1_c_out[1]), .Preset_7(undriven_10), .C_Out(registrador_1_c_out[0]));
  Hex_Digit_Display hex_digit_display_1 (.value(registrador_1_q3));  // open: dp
  Clock clock_1 (.out(clock_1_out));
  Shift_Register B (
    .in(1'b0), .clk(clock_1_out), .out(B_out), .q0(B_q3[3]), .q1(B_q3[2]), .q2(B_q3[1]), .q3(B_q3[0]),
    .q4(B_q7[3]), .q5(B_q7[2]), .q6(B_q7[1]), .q7(B_q7[0]));  // open: shift, load, clr, d0, d1, d2, d3, d4, d5, d6, d7
  Hex_Digit_Display hex_digit_display_2 (.value(registrador_1_c_out));  // open: dp
  registrador registrador_2 (
    .C_In(mux_1_output), .Clear(clear), .Clock(clock_1_out), .Preset_0(in_2[0]), .Q0(registrador_2_q3[3]),
    .Preset_1(in_2[1]), .Q1(registrador_2_q3[2]), .Preset_2(in_2[2]), .Q2(registrador_2_q3[1]),
    .Preset_3(in_2[3]), .Q3(registrador_2_q3[0]), .Preset_4(in_2[4]), .Q4(registrador_2_c_out[3]),
    .Preset_5(in_2[5]), .Q5(registrador_2_c_out[2]), .Preset_6(in_2[6]), .Q6(registrador_2_c_out[1]),
    .Preset_7(in_2[7]), .C_Out(registrador_2_c_out[0]));
  xor xor_1 (xor_1_out, B_out, Binvert);
  Hex_Digit_Display hex_digit_display_3 (.value(registrador_2_q3));  // open: dp
  Hex_Digit_Display hex_digit_display_4 (.value(registrador_2_c_out));  // open: dp
  Hex_Digit_Display hex_digit_display_5 (.value(B_q3));  // open: dp
  and and_1 (and_1_out, registrador_2_c_out[0], B_out);
  or or_1 (or_1_out, registrador_2_c_out[0], B_out);
  xor xor_2 (xor_2_out, registrador_2_c_out[0], B_out);
  Hex_Digit_Display hex_digit_display_6 (.value(B_q7));  // open: dp
  Adder #(.width(1)) adder_1 (
    .a(registrador_2_c_out[0]), .b(xor_1_out), .out(adder_1_out), .cin(Carry_q), .cout(adder_1_cout));
  D_Flip_Flop Carry (.clk(clock_1_out), .D(adder_1_cout), .Q(Carry_q));  // open: Qn, preset, en, reset
  mux mux_1 (.S0(S0), .S1(S1), .D0(and_1_out), .D1(or_1_out), .D2(xor_2_out), .D3(adder_1_out), .Output(mux_1_output));
endmodule

module registrador (
  input  Clock,
  input  C_In,
  input  Preset_0,
  input  Preset_1,
  input  Preset_2,
  input  Preset_3,
  input  Preset_4,
  input  Preset_5,
  input  Preset_6,
  input  Preset_7,
  input  Clear,
  output C_Out,
  output Q0,
  output Q1,
  output Q2,
  output Q3,
  output Q4,
  output Q5,
  output Q6
);

  D_Flip_Flop d_ff_1 (.clk(Clock), .D(C_In), .Q(Q0), .preset(Preset_0), .reset(Clear));  // open: Qn, en
  D_Flip_Flop d_ff_2 (.clk(Clock), .D(Q0), .Q(Q1), .preset(Preset_1), .reset(Clear));  // open: Qn, en
  D_Flip_Flop d_ff_3 (.clk(Clock), .D(Q1), .Q(Q2), .preset(Preset_2), .reset(Clear));  // open: Qn, en
  D_Flip_Flop d_ff_4 (.clk(Clock), .D(Q2), .Q(Q3), .preset(Preset_3), .reset(Clear));  // open: Qn, en
  D_Flip_Flop d_ff_5 (.clk(Clock), .D(Q3), .Q(Q4), .preset(Preset_4), .reset(Clear));  // open: Qn, en
  D_Flip_Flop d_ff_6 (.clk(Clock), .D(Q4), .Q(Q5), .preset(Preset_5), .reset(Clear));  // open: Qn, en
  D_Flip_Flop d_ff_7 (.clk(Clock), .D(Q5), .Q(Q6), .preset(Preset_6), .reset(Clear));  // open: Qn, en
  D_Flip_Flop d_ff_8 (.clk(Clock), .D(Q6), .Q(C_Out), .preset(Preset_7), .reset(Clear));  // open: Qn, en
endmodule

module mux (
  input  S0,
  input  S1,
  input  D0,
  input  D1,
  input  D2,
  input  D3,
  output Output
);

  wire and_1_out, and_2_out, and_3_out, and_4_out, not_1_out, not_2_out;

  not not_1 (not_1_out, S1);
  not not_2 (not_2_out, S0);
  and and_1 (and_1_out, not_1_out, D0, not_2_out);
  and and_2 (and_2_out, not_1_out, D1, S0);
  and and_3 (and_3_out, S1, D2, not_2_out);
  and and_4 (and_4_out, S1, D3, S0);
  or or_1 (Output, and_1_out, and_2_out, and_3_out, and_4_out);
endmodule
